# Fritzing sketch encoder (saved by Fritzing 0.9.0b)
breadboards: 1

parts:
  Q1 = LTR-301 [package=ltr-301]
  Q2 = LTR-301 [package=ltr-301]
  R1 = Resistor [tolerance=±20% resistance=10k package=THT]
  R2 = Resistor [tolerance=±5% resistance=10k package=THT]
  Part1 = Arduino Mega 2560 (Rev3)
  R3 = Resistor [tolerance=±5% resistance=1k package=THT]
  D1 = LTE-302 [package=lte-302]  # not connected

nets:
  5V: Q1.C, Q2.C
  N1: Q1.E, R2.Pin_0, Part1.D53
  N2: Q2.E, R1.Pin_0, Part1.D52
  GND: R1.Pin_1, R2.Pin_1, R3.Pin_1

notes:
  Doble fototransitor en uno y Led IR de mouse
